// Logisim project BuscaIncrementa.circ as structural Verilog: 1 circuit, main circuit main
module main (
);

  wire button_1_out, clock_1_out, decoder_1_out0, decoder_1_out1, decoder_1_out2, decoder_2_out0,
       decoder_2_out3;
  wire [1:0] counter_1_q;
  wire [11:0] counter_2_q;
  wire [15:0] ram_1_data, register_1_q;

  Button button_1 (.out(button_1_out));
  Register #(.width(16)) register_1 (
    .D(ram_1_data), .en(decoder_2_out0), .Q(register_1_q), .clk(clock_1_out));  // open: clr
  Clock clock_1 (.out(clock_1_out));
  Hex_Digit_Display hex_digit_display_1 (.value(register_1_q[15:12]));  // open: dp
  Counter #(.width(2), .max('h3)) counter_1 (.Q(counter_1_q), .clk(clock_1_out));  // open: load, D, count, carry, clr
  Hex_Digit_Display hex_digit_display_2 (.value(register_1_q[11:8]));  // open: dp
  Decoder #(.select(4), .enable("false")) decoder_1 (
    .out0(decoder_1_out0), .out1(decoder_1_out1), .out2(decoder_1_out2), .sel(register_1_q[15:12]));  // open: out3, out4, out5, out6, out7, out8, out9, out10, out11, out12, out13, out14, out15
  Decoder #(.select(2), .enable("false")) decoder_2 (
    .out0(decoder_2_out0), .out3(decoder_2_out3), .sel(counter_1_q));  // open: out1, out2
  Hex_Digit_Display hex_digit_display_3 (.value(register_1_q[3:0]));  // open: dp
  Hex_Digit_Display hex_digit_display_4 (.value(register_1_q[7:4]));  // open: dp
  Counter #(.width(12), .max('hfff)) counter_2 (
    .load(1'b0), .count(decoder_2_out3), .Q(counter_2_q), .clk(clock_1_out), .clr(button_1_out));  // open: D, carry
  RAM #(.addrWidth(12), .dataWidth(16), .bus("separate")) ram_1 (
    .addr(counter_2_q), .data(ram_1_data), .str(1'b0), .sel(1'b1), .clk(clock_1_out));  // open: din, ld, clr

  // Notes on the sheet:
  //   RESET
  //   CLOCK
  //   Registrador de Instruções
  //   OpCode
  //   Endereço
  //   Busca de instrução
  //   Incrementa PC
  //   Contador de Programa
endmodule
