// Logisim project CarregaArmazenaSalta3.circ as structural Verilog: 1 circuit, main circuit main
module main (
);

  wire and_1_out, and_2_out, button_1_out, clock_1_out, decoder_1_out1, decoder_1_out2, decoder_1_out3,
       decoder_2_out0, decoder_2_out1, decoder_2_out2, decoder_2_out3, nor_1_out, not_1_out, not_2_out;
  wire [1:0] counter_1_q;
  wire [3:0] ram_1_data, ram_1_data_2, ram_1_data_3, ram_1_data_4;
  wire [11:0] counter_2_q, multiplexer_1_out;
  wire [15:0] register_1_q, register_2_q;
  wire [15:12] undriven;

  Button button_1 (.out(button_1_out));
  Register #(.width(16)) register_1 (
    .D({ram_1_data, ram_1_data_4, ram_1_data_3, ram_1_data_2}), .en(decoder_1_out1), .Q(register_1_q),
    .clk(clock_1_out), .clr(button_1_out));
  Register #(.width(16)) register_2 (
    .D({ram_1_data, ram_1_data_4, ram_1_data_3, ram_1_data_2}), .en(decoder_2_out0), .Q(register_2_q),
    .clk(clock_1_out), .clr(button_1_out));
  Clock clock_1 (.out(clock_1_out));
  Hex_Digit_Display hex_digit_display_1 (.value(register_1_q[15:12]));  // open: dp
  Hex_Digit_Display hex_digit_display_2 (.value(register_2_q[15:12]));  // open: dp
  Counter #(.width(2), .max('h3)) counter_1 (
    .Q(counter_1_q), .clk(clock_1_out), .clr(button_1_out));  // open: load, D, count, carry
  Hex_Digit_Display hex_digit_display_3 (.value(register_1_q[11:8]));  // open: dp
  Hex_Digit_Display hex_digit_display_4 (.value(register_2_q[11:8]));  // open: dp
  Decoder #(.select(4), .disabled(0)) decoder_1 (
    .out1(decoder_1_out1), .out2(decoder_1_out2), .out3(decoder_1_out3), .sel(register_2_q[15:12]),
    .en(not_1_out));  // open: out0, out4, out5, out6, out7, out8, out9, out10, out11, out12, out13, out14, out15
  not not_1 (not_1_out, decoder_2_out0);
  not not_2 (not_2_out, decoder_1_out3);
  Decoder #(.select(2), .enable("false")) decoder_2 (
    .out0(decoder_2_out0), .out1(decoder_2_out1), .out2(decoder_2_out2), .out3(decoder_2_out3),
    .sel(counter_1_q));
  Hex_Digit_Display hex_digit_display_5 (.value(register_1_q[3:0]));  // open: dp
  Hex_Digit_Display hex_digit_display_6 (.value(register_1_q[7:4]));  // open: dp
  Hex_Digit_Display hex_digit_display_7 (.value(register_2_q[7:4]));  // open: dp
  Hex_Digit_Display hex_digit_display_8 (.value(register_2_q[3:0]));  // open: dp
  and and_1 (and_1_out, decoder_1_out3, decoder_2_out3);
  and and_2 (and_2_out, not_2_out, decoder_2_out3);
  nor nor_1 (nor_1_out, decoder_1_out2, decoder_1_out1);
  Counter #(.width(12), .max('hfff)) counter_2 (
    .load(and_1_out), .D(register_2_q[11:0]), .count(and_2_out), .Q(counter_2_q), .clk(clock_1_out),
    .clr(button_1_out));  // open: carry
  Multiplexer #(.width(12), .enable("false")) multiplexer_1 (
    .in0(register_2_q[11:0]), .in1(counter_2_q), .out(multiplexer_1_out), .sel(nor_1_out));
  LED led_1 (.in(decoder_2_out0));
  LED led_2 (.in(decoder_2_out1));
  LED led_3 (.in(decoder_2_out2));
  LED led_4 (.in(decoder_2_out3));
  Hex_Digit_Display hex_digit_display_9 (.value(multiplexer_1_out[11:8]));  // open: dp
  Hex_Digit_Display hex_digit_display_10 (.value(undriven));  // open: dp
  Hex_Digit_Display hex_digit_display_11 (.value(multiplexer_1_out[7:4]));  // open: dp
  Hex_Digit_Display hex_digit_display_12 (.value(multiplexer_1_out[3:0]));  // open: dp
  RAM #(.addrWidth(12), .dataWidth(16), .bus("separate")) ram_1 (
    .addr(multiplexer_1_out), .din(register_1_q),
    .data({ram_1_data, ram_1_data_4, ram_1_data_3, ram_1_data_2}), .str(decoder_1_out2), .sel(1'b1),
    .clk(clock_1_out));  // open: ld, clr
  Hex_Digit_Display hex_digit_display_13 (.value(ram_1_data));  // open: dp
  Hex_Digit_Display hex_digit_display_14 (.value(ram_1_data_3));  // open: dp
  Hex_Digit_Display hex_digit_display_15 (.value(ram_1_data_4));  // open: dp
  Hex_Digit_Display hex_digit_display_16 (.value(ram_1_data_2));  // open: dp

  // Notes on the sheet:
  //   RESET
  //   CLOCK
  //   Acumulador
  //   Registrador de Instruções
  //   OpCode
  //   OpCode
  //   Endereço
  //   Endereço
  //   ver explicação para esta logica em README.md 2021-05-06
  //   Busca de instrução
  //   Atualiza PC
  //   Contador de Programa
  //   Expõe endereço de operando ou PC
  //   Se busca instrução, desabilita outras instruções. Tem que habilitar para buscar operando na memória
  //   Busca de instrução
  //   Executa instrução
  //   Atualiza PC
  //   Endereço Exposto
  //   Dados da memória
endmodule
