// Logisim project CarregaArmazenaSaltaArit5.circ as structural Verilog: 1 circuit, main circuit main
module main (
  input  in_1,
  input  in_2
);

  wire and_1_out, and_2_out, and_3_out, and_4_out, and_5_out, and_6_out, button_1_out, clock_1_out,
       decoder_1_out0, decoder_1_out1, decoder_1_out2, decoder_1_out3, decoder_1_out4, decoder_1_out5,
       decoder_1_out6, decoder_1_out15, decoder_2_out0, decoder_2_out1, decoder_2_out2, decoder_2_out3,
       decoder_2_out6, decoder_3_out0, decoder_3_out1, decoder_3_out2, decoder_3_out3, nor_1_out, not_1_out,
       not_2_out, not_3_out, or_1_out, or_2_out, or_3_out, or_4_out;
  wire [1:0] counter_1_q;
  wire [2:0] register_1_q_3;
  wire [3:0] multiplexer_3_out, multiplexer_3_out_2, multiplexer_3_out_3, multiplexer_3_out_4,
       multiplexer_6_out, multiplexer_6_out_2, multiplexer_6_out_3, multiplexer_6_out_4, multiplexer_7_out,
       multiplexer_7_out_2, multiplexer_7_out_3, multiplexer_7_out_4, ram_1_data, ram_1_data_2, ram_1_data_4,
       register_2_q, register_2_q_2, register_2_q_3, register_2_q_4, register_6_q, register_6_q_2,
       register_6_q_3;
  wire [8:0] register_1_q;
  wire [11:0] adder_1_out, counter_2_q, multiplexer_2_out, multiplexer_4_out, multiplexer_5_out;
  wire [11:8] ram_1_data_3;
  wire [15:0] adder_2_out, and_7_out, multiplexer_1_out, not_4_out, or_5_out, register_3_q, register_4_q,
       register_5_q, register_7_q, subtractor_1_out, xor_1_out;
  wire [15:11] comparator_1_gt;
  wire [15:12] register_1_q_2;
  wire [19:0] counter_3_q;

  Clock clock_1 (.out(clock_1_out));
  and and_1 (and_1_out, not_1_out, clock_1_out);
  Hex_Digit_Display hex_digit_display_1 (.value(register_2_q_4));  // open: dp
  Hex_Digit_Display hex_digit_display_2 (.value(register_2_q_3));  // open: dp
  and and_2 (and_2_out, decoder_3_out1, decoder_1_out6);
  Button button_1 (.out(button_1_out));
  Hex_Digit_Display hex_digit_display_3 (.value(register_2_q_2));  // open: dp
  Hex_Digit_Display hex_digit_display_4 (.value(register_2_q));  // open: dp
  Register #(.width(16)) register_1 (
    .D({ram_1_data_4, ram_1_data_3, ram_1_data_2, ram_1_data}), .en(decoder_3_out0),
    .Q({register_1_q_2, register_1_q_3, register_1_q}), .clk(and_1_out), .clr(button_1_out));
  not not_1 (not_1_out, decoder_1_out15);
  Hex_Digit_Display hex_digit_display_5 (.value(register_1_q_2));  // open: dp
  Decoder #(.select(4), .disabled(0)) decoder_1 (
    .out0(decoder_1_out0), .out1(decoder_1_out1), .out2(decoder_1_out2), .out3(decoder_1_out3),
    .out4(decoder_1_out4), .out5(decoder_1_out5), .out6(decoder_1_out6), .out15(decoder_1_out15),
    .sel(register_1_q_2), .en(not_2_out));  // open: out7, out8, out9, out10, out11, out12, out13, out14
  not not_2 (not_2_out, decoder_3_out0);
  Counter #(.width(2), .max('h3)) counter_1 (
    .Q(counter_1_q), .clk(and_1_out), .clr(button_1_out));  // open: load, D, count, carry
  Multiplexer #(.width(16), .disabled(0), .enable("false")) multiplexer_1 (
    .in0({multiplexer_7_out, multiplexer_7_out_4, multiplexer_7_out_3, multiplexer_7_out_2}),
    .in1({ram_1_data_4, ram_1_data_3, ram_1_data_2, ram_1_data}), .out(multiplexer_1_out),
    .sel(decoder_1_out1));
  Decoder #(.select(3), .disabled(0)) decoder_2 (
    .out0(decoder_2_out0), .out1(decoder_2_out1), .out2(decoder_2_out2), .out3(decoder_2_out3),
    .out6(decoder_2_out6), .sel(register_1_q[8:6]), .en(and_2_out));  // open: out4, out5, out7
  Hex_Digit_Display hex_digit_display_6 (.value({register_1_q_3, register_1_q[8]}));  // open: dp
  Hex_Digit_Display hex_digit_display_7 (.value(register_1_q[7:4]));  // open: dp
  not not_3 (not_3_out, or_2_out);
  Decoder #(.select(2), .enable("false")) decoder_3 (
    .out0(decoder_3_out0), .out1(decoder_3_out1), .out2(decoder_3_out2), .out3(decoder_3_out3),
    .sel(counter_1_q));
  or or_1 (or_1_out, decoder_1_out1, decoder_2_out0);
  Hex_Digit_Display hex_digit_display_8 (.value(register_1_q[3:0]));  // open: dp
  or or_2 (or_2_out, decoder_1_out5, decoder_1_out3, and_6_out);
  Multiplexer #(.width(12), .enable("false")) multiplexer_2 (
    .in0({register_1_q_3, register_1_q}), .in1({register_6_q_3, register_6_q_2, register_6_q}),
    .out(multiplexer_2_out), .sel(decoder_1_out5));
  and and_3 (and_3_out, or_2_out, decoder_3_out3);
  and and_4 (and_4_out, not_3_out, decoder_3_out3);
  Register #(.width(16)) register_2 (
    .D(multiplexer_1_out), .en(or_1_out), .Q({register_2_q_4, register_2_q_3, register_2_q_2, register_2_q}),
    .clk(and_1_out), .clr(button_1_out));
  Register #(.width(16)) register_3 (
    .D({multiplexer_7_out, multiplexer_7_out_4, multiplexer_7_out_3, multiplexer_7_out_2}),
    .en(decoder_2_out1), .Q(register_3_q), .clk(and_1_out), .clr(button_1_out));
  Register #(.width(16)) register_4 (
    .D({multiplexer_7_out, multiplexer_7_out_4, multiplexer_7_out_3, multiplexer_7_out_2}),
    .en(decoder_2_out2), .Q(register_4_q), .clk(and_1_out), .clr(button_1_out));
  Register #(.width(16)) register_5 (
    .D({multiplexer_7_out, multiplexer_7_out_4, multiplexer_7_out_3, multiplexer_7_out_2}),
    .en(decoder_2_out3), .Q(register_5_q), .clk(and_1_out), .clr(button_1_out));
  nor nor_1 (nor_1_out, decoder_1_out2, decoder_1_out1);
  and and_5 (and_5_out, or_2_out, decoder_3_out3);
  Counter #(.width(12), .max('hfff)) counter_2 (
    .load(and_3_out), .D(multiplexer_2_out), .count(and_4_out), .Q(counter_2_q), .clk(and_1_out),
    .clr(button_1_out));  // open: carry
  Multiplexer #(.select(3), .width(16), .disabled(0), .enable("false")) multiplexer_3 (
    .in0({register_2_q_4, register_2_q_3, register_2_q_2, register_2_q}), .in1(register_3_q),
    .in2(register_4_q), .in3(register_5_q), .in4({16{1'b0}}), .in5({16{1'b0}}),
    .in6({4'b0000, register_6_q_3, register_6_q_2, register_6_q}), .in7(register_7_q),
    .out({multiplexer_3_out, multiplexer_3_out_4, multiplexer_3_out_3, multiplexer_3_out_2}),
    .sel(register_1_q[5:3]));
  or or_3 (or_3_out, register_2_q_4[3], register_2_q_4[2], register_2_q_4[1], register_2_q_4[0], register_2_q_3[3], register_2_q_3[2], register_2_q_3[1], register_2_q_3[0], register_2_q_2[2], register_2_q_2[1], register_2_q_2[0], register_2_q[3], register_2_q[2], register_2_q[1], register_2_q[0], register_2_q_2[3]);
  and and_6 (and_6_out, decoder_1_out4, or_3_out);
  Multiplexer #(.width(12), .enable("false")) multiplexer_4 (
    .in0({register_1_q_3, register_1_q}), .in1(counter_2_q), .out(multiplexer_4_out), .sel(nor_1_out));
  Adder #(.width(12)) adder_1 (.a({12{1'b0}}), .b(counter_2_q), .out(adder_1_out), .cin(1'b1));  // open: cout
  LED led_1 (.in(decoder_3_out0));
  LED led_2 (.in(decoder_3_out1));
  LED led_3 (.in(decoder_3_out2));
  LED led_4 (.in(decoder_3_out3));
  Multiplexer #(.width(12), .enable("false")) multiplexer_5 (
    .in0(adder_1_out), .in1({multiplexer_7_out_4, multiplexer_7_out_3, multiplexer_7_out_2}),
    .out(multiplexer_5_out), .sel(decoder_2_out6));
  or or_4 (or_4_out, decoder_2_out6, and_5_out);
  Register #(.width(12)) register_6 (
    .D(multiplexer_5_out), .en(or_4_out), .Q({register_6_q_3, register_6_q_2, register_6_q}),
    .clk(and_1_out), .clr(button_1_out));
  Multiplexer #(.select(2), .width(16), .disabled(0)) multiplexer_6 (
    .in0({register_2_q_4, register_2_q_3, register_2_q_2, register_2_q}), .in1(register_3_q),
    .in2(register_4_q), .in3(register_5_q),
    .out({multiplexer_6_out, multiplexer_6_out_4, multiplexer_6_out_3, multiplexer_6_out_2}),
    .sel(register_1_q[1:0]), .en(register_1_q[2]));
  Hex_Digit_Display hex_digit_display_9 (.value(register_6_q_3));  // open: dp
  Hex_Digit_Display hex_digit_display_10 (.value(multiplexer_3_out));  // open: dp
  Hex_Digit_Display hex_digit_display_11 (.value(multiplexer_6_out));  // open: dp
  Hex_Digit_Display hex_digit_display_12 (.value(register_6_q_2));  // open: dp
  Hex_Digit_Display hex_digit_display_13 (.value(multiplexer_3_out_4));  // open: dp
  Hex_Digit_Display hex_digit_display_14 (.value(multiplexer_6_out_4));  // open: dp
  Hex_Digit_Display hex_digit_display_15 (.value(register_6_q));  // open: dp
  Hex_Digit_Display hex_digit_display_16 (.value(multiplexer_3_out_3));  // open: dp
  Hex_Digit_Display hex_digit_display_17 (.value(multiplexer_3_out_2));  // open: dp
  Hex_Digit_Display hex_digit_display_18 (.value(multiplexer_6_out_3));  // open: dp
  Hex_Digit_Display hex_digit_display_19 (.value(multiplexer_6_out_2));  // open: dp
  Hex_Digit_Display hex_digit_display_20 (.value(multiplexer_4_out[11:8]));  // open: dp
  Hex_Digit_Display hex_digit_display_21 (.value(multiplexer_4_out[3:0]));  // open: dp
  Hex_Digit_Display hex_digit_display_22 (.value(multiplexer_4_out[7:4]));  // open: dp
  Counter #(.width(20), .max('hfffff)) counter_3 (
    .Q(counter_3_q), .clk(and_1_out), .clr(button_1_out));  // open: load, D, count, carry
  assign not_4_out = ~{multiplexer_3_out, multiplexer_3_out_4, multiplexer_3_out_3, multiplexer_3_out_2};  // NOT_Gate not_4, 16 bits wide
  Hex_Digit_Display hex_digit_display_23 (.value(counter_3_q[19:16]));  // open: dp
  Hex_Digit_Display hex_digit_display_24 (.value(counter_3_q[15:12]));  // open: dp
  Multiplexer #(.select(3), .width(16), .disabled(0), .enable("false")) multiplexer_7 (
    .in0({16{1'b0}}), .in1({16{1'b1}}), .in2(not_4_out), .in3(and_7_out), .in4(or_5_out), .in5(xor_1_out),
    .in6(adder_2_out), .in7(subtractor_1_out),
    .out({multiplexer_7_out, multiplexer_7_out_4, multiplexer_7_out_3, multiplexer_7_out_2}),
    .sel(register_1_q_3));
  assign and_7_out = {multiplexer_3_out, multiplexer_3_out_4, multiplexer_3_out_3, multiplexer_3_out_2} & {multiplexer_6_out, multiplexer_6_out_4, multiplexer_6_out_3, multiplexer_6_out_2};  // AND_Gate and_7, 16 bits wide
  Hex_Digit_Display hex_digit_display_25 (.value(counter_3_q[11:8]));  // open: dp
  assign or_5_out = {multiplexer_3_out, multiplexer_3_out_4, multiplexer_3_out_3, multiplexer_3_out_2} | {multiplexer_6_out, multiplexer_6_out_4, multiplexer_6_out_3, multiplexer_6_out_2};  // OR_Gate or_5, 16 bits wide
  Hex_Digit_Display hex_digit_display_26 (.value(ram_1_data_4));  // open: dp
  Hex_Digit_Display hex_digit_display_27 (.value(counter_3_q[7:4]));  // open: dp
  Hex_Digit_Display hex_digit_display_28 (.value(counter_3_q[3:0]));  // open: dp
  Hex_Digit_Display hex_digit_display_29 (.value(multiplexer_7_out));  // open: dp
  assign xor_1_out = {multiplexer_3_out, multiplexer_3_out_4, multiplexer_3_out_3, multiplexer_3_out_2} ^ {multiplexer_6_out, multiplexer_6_out_4, multiplexer_6_out_3, multiplexer_6_out_2};  // XOR_Gate xor_1, 16 bits wide
  Hex_Digit_Display hex_digit_display_30 (.value(ram_1_data_3));  // open: dp
  Hex_Digit_Display hex_digit_display_31 (.value(multiplexer_7_out_3));  // open: dp
  Hex_Digit_Display hex_digit_display_32 (.value(multiplexer_7_out_4));  // open: dp
  Adder #(.width(16)) adder_2 (
    .a({multiplexer_3_out, multiplexer_3_out_4, multiplexer_3_out_3, multiplexer_3_out_2}),
    .b({multiplexer_6_out, multiplexer_6_out_4, multiplexer_6_out_3, multiplexer_6_out_2}),
    .out(adder_2_out), .cin(1'b0), .cout(comparator_1_gt[15]));
  Hex_Digit_Display hex_digit_display_33 (.value(ram_1_data));  // open: dp
  Hex_Digit_Display hex_digit_display_34 (.value(ram_1_data_2));  // open: dp
  Hex_Digit_Display hex_digit_display_35 (.value(multiplexer_7_out_2));  // open: dp
  Subtractor #(.width(16)) subtractor_1 (
    .a({multiplexer_3_out, multiplexer_3_out_4, multiplexer_3_out_3, multiplexer_3_out_2}),
    .b({multiplexer_6_out, multiplexer_6_out_4, multiplexer_6_out_3, multiplexer_6_out_2}),
    .out(subtractor_1_out), .bin(1'b0), .bout(comparator_1_gt[14]));
  RAM #(.addrWidth(12), .dataWidth(16), .bus("separate")) ram_1 (
    .addr(multiplexer_4_out), .din({register_2_q_4, register_2_q_3, register_2_q_2, register_2_q}),
    .data({ram_1_data_4, ram_1_data_3, ram_1_data_2, ram_1_data}), .str(decoder_1_out2), .sel(1'b1),
    .clk(and_1_out));  // open: ld, clr
  Comparator #(.width(16), .mode("unsigned")) comparator_1 (
    .a({multiplexer_3_out, multiplexer_3_out_4, multiplexer_3_out_3, multiplexer_3_out_2}),
    .b({multiplexer_6_out, multiplexer_6_out_4, multiplexer_6_out_3, multiplexer_6_out_2}),
    .gt(comparator_1_gt[11]), .eq(comparator_1_gt[12]), .lt(comparator_1_gt[13]));
  Register #(.width(16)) register_7 (
    .D({comparator_1_gt, {3{in_2}}, in_1, {3{in_2}}, in_1, {3{in_2}}}), .en(and_2_out), .Q(register_7_q),
    .clk(and_1_out), .clr(button_1_out));

  // Notes on the sheet:
  //   CLOCK
  //   Registrador de Instruções
  //   RESET
  //   Resultado ou memória
  //   Executa op. arit
  //   ARIT
  //   Executa Instrução
  //   Acumulador
  //   ARIT
  //   OpCode
  //   registrador que armazena o resultado(3)
  //   operando A (3)
  //   Endereço
  //   NOP
  //   RET
  //   ARIT
  //   usar operando B de registrador(1)
  //   operando B(2)
  //   CLOCK
  //   RESET
  //   LDA
  //   JNZ
  //   ver explicação para esta logica em README.md 2021-05-06
  //   Busca de instrução
  //   Acumulador
  //   Endereço de Retorno 
  //   operação(3)
  //   STA
  //   Atualiza PC
  //   Expõe endereço de operando ou PC
  //   Se busca instrução, desabilita outras instruções. Tem que habilitar para buscar operando na memória
  //   Contador de Programa
  //   Se for Jump e for atualizar o PC
  //   RES:RESultado
  //   eRP:Enable RPilha
  //   *RP
  //   eRP
  //   Se for Jump lê endereço do operando, se for RET lê endereço do registrador de mais recente.
  //   Busca de instrução
  //   Executa instrução
  //   Atualiza PC
  //   RES
  //   *RP
  //   Operando A
  //   Operando B
  //   clock
  //   mostra o endereço do comando Jump executado mais recentemente.
  //   Conta quantos ciclos de clock passaram.
  //   Resultado
  //   PSW atualiza em toda execução de operação aritmética
  //   Dados da memória
  //   PSW e Interrupções
  //   Apenas para atribuir algum valor a esses pinos
endmodule
