// Logisim project CarregaArmazenaSaltaSeFFFF2.circ as structural Verilog: 1 circuit, main circuit main
module main (
);

  wire and_1_out, and_2_out, and_3_out, button_1_out, clock_1_out, decoder_1_out0, decoder_1_out1,
       decoder_1_out2, decoder_1_out3, decoder_1_out4, decoder_2_out0, decoder_2_out1, decoder_2_out2,
       decoder_2_out3, nor_1_out, not_1_out, not_2_out, or_1_out;
  wire [1:0] counter_1_q;
  wire [11:0] counter_2_q, multiplexer_1_out;
  wire [15:0] ram_1_data, register_1_q, register_2_q;

  Button button_1 (.out(button_1_out));
  Register #(.width(16)) register_1 (
    .D(ram_1_data), .en(decoder_1_out1), .Q(register_1_q), .clk(clock_1_out), .clr(button_1_out));
  Register #(.width(16)) register_2 (
    .D(ram_1_data), .en(decoder_2_out0), .Q(register_2_q), .clk(clock_1_out), .clr(button_1_out));
  Clock clock_1 (.out(clock_1_out));
  Hex_Digit_Display hex_digit_display_1 (.value(register_1_q[15:12]));  // open: dp
  Hex_Digit_Display hex_digit_display_2 (.value(register_2_q[15:12]));  // open: dp
  Counter #(.width(2), .max('h3)) counter_1 (
    .Q(counter_1_q), .clk(clock_1_out), .clr(button_1_out));  // open: load, D, count, carry
  Hex_Digit_Display hex_digit_display_3 (.value(register_1_q[11:8]));  // open: dp
  Hex_Digit_Display hex_digit_display_4 (.value(register_2_q[11:8]));  // open: dp
  Decoder #(.select(4), .disabled(0)) decoder_1 (
    .out0(decoder_1_out0), .out1(decoder_1_out1), .out2(decoder_1_out2), .out3(decoder_1_out3),
    .out4(decoder_1_out4), .sel(register_2_q[15:12]), .en(not_1_out));  // open: out5, out6, out7, out8, out9, out10, out11, out12, out13, out14, out15
  not not_1 (not_1_out, decoder_2_out0);
  Decoder #(.select(2), .enable("false")) decoder_2 (
    .out0(decoder_2_out0), .out1(decoder_2_out1), .out2(decoder_2_out2), .out3(decoder_2_out3),
    .sel(counter_1_q));
  Hex_Digit_Display hex_digit_display_5 (.value(register_1_q[7:4]));  // open: dp
  Hex_Digit_Display hex_digit_display_6 (.value(register_1_q[3:0]));  // open: dp
  Hex_Digit_Display hex_digit_display_7 (.value(register_2_q[7:4]));  // open: dp
  Hex_Digit_Display hex_digit_display_8 (.value(register_2_q[3:0]));  // open: dp
  or or_1 (or_1_out, decoder_1_out3, and_3_out);
  and and_1 (and_1_out, or_1_out, decoder_2_out3);
  not not_2 (not_2_out, or_1_out);
  and and_2 (and_2_out, not_2_out, decoder_2_out3);
  nor nor_1 (nor_1_out, decoder_1_out2, decoder_1_out1);
  Counter #(.width(12), .max('hfff)) counter_2 (
    .load(and_1_out), .D(register_2_q[11:0]), .count(and_2_out), .Q(counter_2_q), .clk(clock_1_out),
    .clr(button_1_out));  // open: carry
  and and_3 (and_3_out, decoder_1_out4, register_1_q[15], register_1_q[14], register_1_q[13], register_1_q[12], register_1_q[11], register_1_q[10], register_1_q[9], register_1_q[8], register_1_q[7], register_1_q[6], register_1_q[5], register_1_q[4], register_1_q[3], register_1_q[2], register_1_q[1], register_1_q[0]);
  Multiplexer #(.width(12), .enable("false")) multiplexer_1 (
    .in0(register_2_q[11:0]), .in1(counter_2_q), .out(multiplexer_1_out), .sel(nor_1_out));
  LED led_1 (.in(decoder_2_out0));
  LED led_2 (.in(decoder_2_out1));
  LED led_3 (.in(decoder_2_out2));
  LED led_4 (.in(decoder_2_out3));
  Hex_Digit_Display hex_digit_display_9 (.value(multiplexer_1_out[11:8]));  // open: dp
  Hex_Digit_Display hex_digit_display_10 (.value(multiplexer_1_out[7:4]));  // open: dp
  Hex_Digit_Display hex_digit_display_11 (.value(multiplexer_1_out[3:0]));  // open: dp
  RAM #(.addrWidth(12), .dataWidth(16), .bus("separate")) ram_1 (
    .addr(multiplexer_1_out), .din(register_1_q), .data(ram_1_data), .str(decoder_1_out2), .sel(1'b1),
    .clk(clock_1_out));  // open: ld, clr
  Hex_Digit_Display hex_digit_display_12 (.value(ram_1_data[15:12]));  // open: dp
  Hex_Digit_Display hex_digit_display_13 (.value(ram_1_data[7:4]));  // open: dp
  Hex_Digit_Display hex_digit_display_14 (.value(ram_1_data[11:8]));  // open: dp
  Hex_Digit_Display hex_digit_display_15 (.value(ram_1_data[3:0]));  // open: dp

  // Notes on the sheet:
  //   RESET
  //   CLOCK
  //   Acumulador
  //   Registrador de Instruções
  //   OpCode
  //   NOP
  //   Endereço
  //   LDA
  //   JF
  //   ver explicação para esta logica em README.md 2021-05-06
  //   Busca de instrução
  //   STA
  //   Atualiza PC
  //   Expõe endereço de operando ou PC
  //   Se busca instrução, desabilita outras instruções. Tem que habilitar para buscar operando na memória
  //   Contador de Programa
  //   Endereço Exposto
  //   Busca de instrução
  //   Executa instrução
  //   Atualiza PC
  //   O salto se FFFF funciona, agora implementar o registro do endereço de retorno
  //   Dados da memória
endmodule
