// Logisim project Endereca.circ as structural Verilog: 1 circuit, main circuit main
module main (
);

  wire button_1_out, clock_1_out, decoder_1_out0, decoder_1_out1, decoder_2_out0, decoder_2_out1,
       decoder_2_out2, decoder_2_out3, not_1_out, not_2_out;
  wire [1:0] counter_1_q;
  wire [3:0] ram_1_data_2, ram_1_data_3;
  wire [11:0] counter_2_q;
  wire [11:8] ram_1_data_4;
  wire [15:0] register_1_q, undriven;
  wire [15:12] ram_1_data;

  Button button_1 (.out(button_1_out));
  Register #(.width(16)) register_1 (
    .D({ram_1_data, ram_1_data_4, ram_1_data_3, ram_1_data_2}), .en(decoder_2_out0), .Q(register_1_q),
    .clk(clock_1_out), .clr(button_1_out));
  Clock clock_1 (.out(clock_1_out));
  Hex_Digit_Display hex_digit_display_1 (.value(register_1_q[15:12]));  // open: dp
  Counter #(.width(2), .max('h3)) counter_1 (
    .Q(counter_1_q), .clk(clock_1_out), .clr(button_1_out));  // open: load, D, count, carry
  Hex_Digit_Display hex_digit_display_2 (.value(undriven[15:12]));  // open: dp
  Hex_Digit_Display hex_digit_display_3 (.value(register_1_q[11:8]));  // open: dp
  Decoder #(.select(4), .disabled(0)) decoder_1 (
    .out0(decoder_1_out0), .out1(decoder_1_out1), .sel(register_1_q[15:12]), .en(not_1_out));  // open: out2, out3, out4, out5, out6, out7, out8, out9, out10, out11, out12, out13, out14, out15
  not not_1 (not_1_out, decoder_2_out0);
  Decoder #(.select(2), .enable("false")) decoder_2 (
    .out0(decoder_2_out0), .out1(decoder_2_out1), .out2(decoder_2_out2), .out3(decoder_2_out3),
    .sel(counter_1_q));
  Hex_Digit_Display hex_digit_display_4 (.value(undriven[11:8]));  // open: dp
  Hex_Digit_Display hex_digit_display_5 (.value(undriven[7:4]));  // open: dp
  Hex_Digit_Display hex_digit_display_6 (.value(register_1_q[7:4]));  // open: dp
  Hex_Digit_Display hex_digit_display_7 (.value(register_1_q[3:0]));  // open: dp
  Hex_Digit_Display hex_digit_display_8 (.value(undriven[3:0]));  // open: dp
  not not_2 (not_2_out, decoder_1_out1);
  Counter #(.width(12), .max('hfff)) counter_2 (
    .load(1'b0), .count(decoder_2_out3), .Q(counter_2_q), .clk(clock_1_out), .clr(button_1_out));  // open: D, carry
  Multiplexer #(.width(12), .enable("false")) multiplexer_1 (
    .in0(register_1_q[11:0]), .in1(counter_2_q), .out(undriven[11:0]), .sel(not_2_out));
  LED led_1 (.in(decoder_2_out0));
  LED led_2 (.in(decoder_2_out1));
  LED led_3 (.in(decoder_2_out2));
  LED led_4 (.in(decoder_2_out3));
  RAM #(.addrWidth(12), .dataWidth(16), .bus("separate")) ram_1 (
    .addr(undriven[11:0]), .data({ram_1_data, ram_1_data_4, ram_1_data_3, ram_1_data_2}), .str(1'b0),
    .sel(1'b1), .clk(clock_1_out));  // open: din, ld, clr
  Hex_Digit_Display hex_digit_display_9 (.value(ram_1_data));  // open: dp
  Hex_Digit_Display hex_digit_display_10 (.value(ram_1_data_4));  // open: dp
  Hex_Digit_Display hex_digit_display_11 (.value(ram_1_data_3));  // open: dp
  Hex_Digit_Display hex_digit_display_12 (.value(ram_1_data_2));  // open: dp

  // Notes on the sheet:
  //   RESET
  //   CLOCK
  //   Registrador de Instruções
  //   OpCode
  //   Endereço
  //   Endereço exposto no barramento de endereço
  //   Busca de instrução
  //   sSe busca instrução, desabilita outras instruções
  //   Contador de Programa
  //   Expõe endereço de operando ou PC
  //   Na borda de subida incrementa PC
  //   Dados da memória
  //   Ainda não faz nada, mas como a instrução é a que está carregada no RI, o endereço exposto no barramento é ajustado de acordo
  //   Busca de instrução (antes da borda de subida coloca o conteúdo do CP no barramento de endereçamento, na borda de subida armazena o conteúdo da memória (M(CP)) no registrador de instrução
  //   Se a instrução for 0x1XXX, Busca valor de operando imediato (antes da borda de subida coloca os 12 bits de endereço contidos na instrução no barramento de endereçamento, ainda não faz nada na borda de subida
endmodule
