// Logisim project LogicaEAritmetica-projeto.circ as structural Verilog: 1 circuit, main circuit main
module main (
  input  [1:0] in_1,
  input  [2:0] in_2,
  input  [2:0] operando_A,
  input  operando_B,
  input  [1:0] in_5,
  input  [2:0] \operação 
);

  wire button_1_out, clock_1_out, decoder_1_out0, decoder_1_out1, decoder_1_out2, decoder_1_out3;
  wire [3:0] multiplexer_2_out, multiplexer_2_out_2, multiplexer_2_out_3, multiplexer_2_out_4,
       multiplexer_3_out, multiplexer_3_out_2, multiplexer_3_out_3, multiplexer_3_out_4, multiplexer_4_out,
       multiplexer_4_out_2, multiplexer_4_out_3, multiplexer_4_out_4;
  wire [15:0] adder_1_out, and_1_out, multiplexer_1_out, not_1_out, or_1_out, register_1_q, register_2_q,
       register_3_q, register_4_q, register_5_q, subtractor_1_out, undriven, undriven_2, undriven_3,
       undriven_4, xor_1_out;

  Multiplexer #(.select(2), .width(16)) multiplexer_1 (
    .in0({multiplexer_4_out, multiplexer_4_out_4, multiplexer_4_out_3, multiplexer_4_out_2}), .in1(undriven),
    .in2(undriven_2), .in3(undriven_3), .out(multiplexer_1_out), .sel(in_1));  // open: en
  Decoder #(.select(3)) decoder_1 (
    .out0(decoder_1_out0), .out1(decoder_1_out1), .out2(decoder_1_out2), .out3(decoder_1_out3), .sel(in_2));  // open: out4, out5, out6, out7, en
  Register #(.width(16)) register_1 (
    .D(multiplexer_1_out), .en(decoder_1_out0), .Q(register_1_q), .clk(clock_1_out), .clr(button_1_out));
  Register #(.width(16)) register_2 (
    .D({multiplexer_4_out, multiplexer_4_out_4, multiplexer_4_out_3, multiplexer_4_out_2}),
    .en(decoder_1_out1), .Q(register_2_q), .clk(clock_1_out), .clr(button_1_out));
  Register #(.width(16)) register_3 (
    .D({multiplexer_4_out, multiplexer_4_out_4, multiplexer_4_out_3, multiplexer_4_out_2}),
    .en(decoder_1_out2), .Q(register_3_q), .clk(clock_1_out), .clr(button_1_out));
  Register #(.width(16)) register_4 (
    .D({multiplexer_4_out, multiplexer_4_out_4, multiplexer_4_out_3, multiplexer_4_out_2}),
    .en(decoder_1_out3), .Q(register_4_q), .clk(clock_1_out), .clr(button_1_out));
  Clock clock_1 (.out(clock_1_out));
  Button button_1 (.out(button_1_out));
  Multiplexer #(.select(3), .width(16), .disabled(0), .enable("false")) multiplexer_2 (
    .in0(register_1_q), .in1(register_2_q), .in2(register_3_q), .in3(register_4_q),
    .out({multiplexer_2_out, multiplexer_2_out_4, multiplexer_2_out_3, multiplexer_2_out_2}), .sel(operando_A));  // open: in4, in5, in6, in7
  Multiplexer #(.select(2), .width(16)) multiplexer_3 (
    .in0(register_1_q), .in1(register_2_q), .in2(register_3_q), .in3(register_4_q),
    .out({multiplexer_3_out_4, multiplexer_3_out_3, multiplexer_3_out_2, multiplexer_3_out}), .sel(in_5),
    .en(operando_B));
  Hex_Digit_Display hex_digit_display_1 (.value(multiplexer_4_out));  // open: dp
  Hex_Digit_Display hex_digit_display_2 (.value(multiplexer_2_out));  // open: dp
  Hex_Digit_Display hex_digit_display_3 (.value(multiplexer_3_out_4));  // open: dp
  Hex_Digit_Display hex_digit_display_4 (.value(multiplexer_4_out_4));  // open: dp
  Hex_Digit_Display hex_digit_display_5 (.value(multiplexer_4_out_3));  // open: dp
  Hex_Digit_Display hex_digit_display_6 (.value(multiplexer_2_out_4));  // open: dp
  Hex_Digit_Display hex_digit_display_7 (.value(multiplexer_2_out_3));  // open: dp
  Hex_Digit_Display hex_digit_display_8 (.value(multiplexer_3_out_3));  // open: dp
  Hex_Digit_Display hex_digit_display_9 (.value(multiplexer_4_out_2));  // open: dp
  Hex_Digit_Display hex_digit_display_10 (.value(multiplexer_2_out_2));  // open: dp
  Hex_Digit_Display hex_digit_display_11 (.value(multiplexer_3_out));  // open: dp
  Hex_Digit_Display hex_digit_display_12 (.value(multiplexer_3_out_2));  // open: dp
  assign not_1_out = ~{multiplexer_2_out, multiplexer_2_out_4, multiplexer_2_out_3, multiplexer_2_out_2};  // NOT_Gate not_1, 16 bits wide
  Multiplexer #(.select(3), .width(16)) multiplexer_4 (
    .in0({16{1'b0}}), .in1({16{1'b1}}), .in2(not_1_out), .in3(and_1_out), .in4(or_1_out), .in5(xor_1_out),
    .in6(adder_1_out), .in7(subtractor_1_out),
    .out({multiplexer_4_out, multiplexer_4_out_4, multiplexer_4_out_3, multiplexer_4_out_2}), .sel(\operação ));  // open: en
  assign and_1_out = {multiplexer_2_out, multiplexer_2_out_4, multiplexer_2_out_3, multiplexer_2_out_2} & {multiplexer_3_out_4, multiplexer_3_out_3, multiplexer_3_out_2, multiplexer_3_out};  // AND_Gate and_1, 16 bits wide
  assign xor_1_out = {multiplexer_2_out, multiplexer_2_out_4, multiplexer_2_out_3, multiplexer_2_out_2} ^ {multiplexer_3_out_4, multiplexer_3_out_3, multiplexer_3_out_2, multiplexer_3_out};  // XOR_Gate xor_1, 16 bits wide
  assign or_1_out = {multiplexer_2_out, multiplexer_2_out_4, multiplexer_2_out_3, multiplexer_2_out_2} | {multiplexer_3_out_4, multiplexer_3_out_3, multiplexer_3_out_2, multiplexer_3_out};  // OR_Gate or_1, 16 bits wide
  Adder #(.width(16)) adder_1 (
    .a({multiplexer_2_out, multiplexer_2_out_4, multiplexer_2_out_3, multiplexer_2_out_2}),
    .b({multiplexer_3_out_4, multiplexer_3_out_3, multiplexer_3_out_2, multiplexer_3_out}),
    .out(adder_1_out), .cout(undriven_4[15]));  // open: cin
  Subtractor #(.width(16)) subtractor_1 (
    .a({multiplexer_2_out, multiplexer_2_out_4, multiplexer_2_out_3, multiplexer_2_out_2}),
    .b({multiplexer_3_out_4, multiplexer_3_out_3, multiplexer_3_out_2, multiplexer_3_out}),
    .out(subtractor_1_out), .bout(undriven_4[14]));  // open: bin
  Register #(.width(16)) register_5 (.D(undriven_4), .Q(register_5_q), .clk(clock_1_out));  // open: en, clr

  // Notes on the sheet:
  //   Memória ou resultado ao acumulador
  //   usar operando B de registrador
  //   registrador que armazena o resultado
  //   O operando A pode ser PSW, PC, Endereço de retorno
  //   Testado 2024-04-10
  //   RESET
  //   Acumulador
  //   Endereço de Retorno 
  //   Resultado
  //   Operando A
  //   Operando B
  //   PSW e Interrupções
endmodule
