// Logisim project apenasConta.circ as structural Verilog: 1 circuit, main circuit main
module main (
);

  wire button_1_out, clock_1_out;
  wire [3:0] ram_1_data_3;
  wire [11:0] ram_1_data_2;
  wire [15:0] undriven;
  wire [15:12] ram_1_data;

  Button button_1 (.out(button_1_out));
  Clock clock_1 (.out(clock_1_out));
  Hex_Digit_Display hex_digit_display_1 (.value(undriven[11:8]));  // open: dp
  Hex_Digit_Display hex_digit_display_2 (.value(undriven[15:12]));  // open: dp
  Hex_Digit_Display hex_digit_display_3 (.value(undriven[7:4]));  // open: dp
  Counter #(.width(12), .max('hfff)) counter_1 (
    .load(1'b0), .count(1'b1), .Q(undriven[11:0]), .clk(clock_1_out), .clr(button_1_out));  // open: D, carry
  Hex_Digit_Display hex_digit_display_4 (.value(undriven[3:0]));  // open: dp
  RAM #(.addrWidth(12), .dataWidth(16), .bus("separate")) ram_1 (
    .addr(undriven[11:0]), .data({ram_1_data, ram_1_data_2[11:8], ram_1_data_3, ram_1_data_2[3:0]}),
    .str(1'b0), .sel(1'b1), .clk(clock_1_out));  // open: din, ld, clr
  Hex_Digit_Display hex_digit_display_5 (.value(ram_1_data));  // open: dp
  Hex_Digit_Display hex_digit_display_6 (.value(ram_1_data_2[11:8]));  // open: dp
  Hex_Digit_Display hex_digit_display_7 (.value(ram_1_data_3));  // open: dp
  Hex_Digit_Display hex_digit_display_8 (.value(ram_1_data_2[3:0]));  // open: dp

  // Notes on the sheet:
  //   Reset
  //   Conta em ordem crescente
  //   Contador de Programa (PC)
  //   o conteúdo do contador fica permanentemente exposto no barramento de endereço, a cada subida do clock o contador é incrementado, isto tem efeito após a subida do clock.
  //   store/write
  //   select
  //   memória carregada com random.mem
endmodule
