// Logisim project carregaInstrucao.circ as structural Verilog: 1 circuit, main circuit main
module main (
);

  wire button_1_out, clock_1_out;
  wire [11:0] counter_1_q;
  wire [15:0] ram_1_data, register_1_q;

  Button button_1 (.out(button_1_out));
  Clock clock_1 (.out(clock_1_out));
  Register #(.width(16)) register_1 (
    .D(ram_1_data), .Q(register_1_q), .clk(clock_1_out), .clr(button_1_out));  // open: en
  Hex_Digit_Display hex_digit_display_1 (.value(register_1_q[11:8]));  // open: dp
  Hex_Digit_Display hex_digit_display_2 (.value(register_1_q[15:12]));  // open: dp
  Decoder #(.select(4), .enable("false")) decoder_1 (.sel(register_1_q[15:12]));  // open: out0, out1, out2, out3, out4, out5, out6, out7, out8, out9, out10, out11, out12, out13, out14, out15
  Hex_Digit_Display hex_digit_display_3 (.value(register_1_q[3:0]));  // open: dp
  Hex_Digit_Display hex_digit_display_4 (.value(register_1_q[7:4]));  // open: dp
  Counter #(.width(12), .max('hfff)) counter_1 (
    .load(1'b0), .count(1'b1), .Q(counter_1_q), .clk(clock_1_out), .clr(button_1_out));  // open: D, carry
  RAM #(.addrWidth(12), .dataWidth(16), .bus("separate")) ram_1 (
    .addr(counter_1_q), .data(ram_1_data), .str(1'b0), .sel(1'b1), .clk(clock_1_out));  // open: din, ld, clr

  // Notes on the sheet:
  //   Reset
  //   Registrador de Instrução
  //   Conta em ordem crescente
  //   OpCode
  //   Contador de Programa (PC)
  //   Operando Direto
  //   store/write
  //   select
  //   o conteúdo do contador fica permanentemente exposto no barramento de endereço, a cada subida do clock o contador é incrementado, isto tem efeito após a subida do clock, então, como simultaneamente o registrador de instrução registra o conteúdo da memória, ele registra o conteúdo anterior à borda do clock.
endmodule
