// Logisim project BancoDeRegistradores.circ as structural Verilog: 1 circuit, main circuit main
module main (
);

  wire decoder_1_out0, decoder_1_out1, decoder_1_out2, decoder_1_out3, undriven_2, undriven_3;
  wire [1:0] undriven, undriven_4;
  wire [15:0] multiplexer_1_out, register_1_q, register_2_q, register_3_q, register_4_q;

  Decoder #(.select(2), .disabled(0)) decoder_1 (
    .out0(decoder_1_out0), .out1(decoder_1_out1), .out2(decoder_1_out2), .out3(decoder_1_out3),
    .sel(undriven), .en(undriven_2));
  Multiplexer #(.select(2), .width(16), .disabled(0)) multiplexer_1 (
    .in0(register_4_q), .in1(register_3_q), .in2(register_2_q), .in3(register_1_q), .out(multiplexer_1_out),
    .sel(undriven_4), .en(undriven_3));
  Register #(.width(16)) register_1 (.D(multiplexer_1_out), .en(decoder_1_out3), .Q(register_1_q));  // open: clk, clr
  Register #(.width(16)) register_2 (.D(multiplexer_1_out), .en(decoder_1_out2), .Q(register_2_q));  // open: clk, clr
  Register #(.width(16)) register_3 (.D(multiplexer_1_out), .en(decoder_1_out1), .Q(register_3_q));  // open: clk, clr
  Register #(.width(16)) register_4 (.D(multiplexer_1_out), .en(decoder_1_out0), .Q(register_4_q));  // open: clk, clr

  // Notes on the sheet:
  //   Seleciona destino
  //   enable
  //   Seleciona origem
endmodule
