// Logisim project CarregaArmazenaSaltaTransfere1.circ as structural Verilog: 1 circuit, main circuit main
module main (
);

  wire and_1_out, and_2_out, button_1_out, clock_1_out, decoder_1_out0, decoder_1_out1, decoder_1_out2,
       decoder_1_out3, decoder_2_out0, decoder_2_out1, decoder_2_out2, decoder_2_out3, decoder_2_out4,
       decoder_3_out0, decoder_3_out1, decoder_3_out2, decoder_3_out3, nor_1_out, not_1_out, not_2_out,
       or_1_out;
  wire [1:0] counter_1_q;
  wire [3:0] multiplexer_3_out, multiplexer_3_out_2, multiplexer_3_out_3, register_1_q, register_2_q_2,
       register_3_q, register_3_q_2, register_4_q, register_4_q_2, register_4_q_3, register_4_q_4,
       register_5_q_2;
  wire [11:0] counter_2_q;
  wire [11:4] register_5_q_3;
  wire [15:0] multiplexer_1_out, multiplexer_2_out, ram_1_data, register_2_q;
  wire [15:4] register_1_q_2;
  wire [15:8] register_3_q_3;
  wire [15:12] register_5_q;

  Decoder #(.select(2), .disabled(0)) decoder_1 (
    .out0(decoder_1_out0), .out1(decoder_1_out1), .out2(decoder_1_out2), .out3(decoder_1_out3),
    .sel(register_5_q_3[11:10]), .en(decoder_2_out4));
  Multiplexer #(.select(2), .width(16), .disabled(0)) multiplexer_1 (
    .in0({register_4_q_4, register_4_q_3, register_4_q_2, register_4_q}),
    .in1({register_3_q_3, register_3_q_2, register_3_q}),
    .in2({register_2_q[15:12], register_2_q_2, register_2_q[7:0]}), .in3({register_1_q_2, register_1_q}),
    .out(multiplexer_1_out), .sel(register_5_q_3[9:8]), .en(register_5_q_3[4]));
  Multiplexer #(.width(16), .enable("false")) multiplexer_2 (
    .in0(multiplexer_1_out), .in1(ram_1_data), .out(multiplexer_2_out), .sel(decoder_2_out1));
  or or_1 (or_1_out, decoder_1_out0, decoder_2_out1);
  Button button_1 (.out(button_1_out));
  Clock clock_1 (.out(clock_1_out));
  Register #(.width(16)) register_1 (
    .D(multiplexer_1_out), .en(decoder_1_out3), .Q({register_1_q_2, register_1_q}), .clk(clock_1_out),
    .clr(button_1_out));
  Register #(.width(16)) register_2 (
    .D(multiplexer_1_out), .en(decoder_1_out2), .Q({register_2_q[15:12], register_2_q_2, register_2_q[7:0]}),
    .clk(clock_1_out), .clr(button_1_out));
  Register #(.width(16)) register_3 (
    .D(multiplexer_1_out), .en(decoder_1_out1), .Q({register_3_q_3, register_3_q_2, register_3_q}),
    .clk(clock_1_out), .clr(button_1_out));
  Register #(.width(16)) register_4 (
    .D(multiplexer_2_out), .en(or_1_out), .Q({register_4_q_4, register_4_q_3, register_4_q_2, register_4_q}),
    .clk(clock_1_out), .clr(button_1_out));
  Register #(.width(16)) register_5 (
    .D(ram_1_data), .en(decoder_3_out0), .Q({register_5_q, register_5_q_3, register_5_q_2}),
    .clk(clock_1_out), .clr(button_1_out));
  Hex_Digit_Display hex_digit_display_1 (.value(register_5_q));  // open: dp
  not not_1 (not_1_out, decoder_3_out0);
  Counter #(.width(2), .max('h3)) counter_1 (
    .Q(counter_1_q), .clk(clock_1_out), .clr(button_1_out));  // open: load, D, count, carry
  Hex_Digit_Display hex_digit_display_2 (.value(register_5_q_3[7:4]));  // open: dp
  Hex_Digit_Display hex_digit_display_3 (.value(register_5_q_3[11:8]));  // open: dp
  Decoder #(.select(4), .disabled(0)) decoder_2 (
    .out0(decoder_2_out0), .out1(decoder_2_out1), .out2(decoder_2_out2), .out3(decoder_2_out3),
    .out4(decoder_2_out4), .sel(register_5_q), .en(not_1_out));  // open: out5, out6, out7, out8, out9, out10, out11, out12, out13, out14, out15
  not not_2 (not_2_out, decoder_2_out3);
  Decoder #(.select(2), .enable("false")) decoder_3 (
    .out0(decoder_3_out0), .out1(decoder_3_out1), .out2(decoder_3_out2), .out3(decoder_3_out3),
    .sel(counter_1_q));
  Hex_Digit_Display hex_digit_display_4 (.value(register_1_q_2[11:8]));  // open: dp
  Hex_Digit_Display hex_digit_display_5 (.value(register_1_q_2[15:12]));  // open: dp
  Hex_Digit_Display hex_digit_display_6 (.value(register_2_q[15:12]));  // open: dp
  Hex_Digit_Display hex_digit_display_7 (.value(register_2_q_2));  // open: dp
  Hex_Digit_Display hex_digit_display_8 (.value(register_3_q_3[15:12]));  // open: dp
  Hex_Digit_Display hex_digit_display_9 (.value(register_3_q_3[11:8]));  // open: dp
  Hex_Digit_Display hex_digit_display_10 (.value(register_5_q_2));  // open: dp
  and and_1 (and_1_out, decoder_2_out3, decoder_3_out3);
  and and_2 (and_2_out, not_2_out, decoder_3_out3);
  Hex_Digit_Display hex_digit_display_11 (.value(register_1_q_2[7:4]));  // open: dp
  Hex_Digit_Display hex_digit_display_12 (.value(register_1_q));  // open: dp
  Hex_Digit_Display hex_digit_display_13 (.value(register_2_q[7:4]));  // open: dp
  Hex_Digit_Display hex_digit_display_14 (.value(register_2_q[3:0]));  // open: dp
  Hex_Digit_Display hex_digit_display_15 (.value(register_3_q_2));  // open: dp
  Hex_Digit_Display hex_digit_display_16 (.value(register_3_q));  // open: dp
  Hex_Digit_Display hex_digit_display_17 (.value(register_4_q_4));  // open: dp
  nor nor_1 (nor_1_out, decoder_2_out2, decoder_2_out1);
  Hex_Digit_Display hex_digit_display_18 (.value(register_4_q_2));  // open: dp
  Hex_Digit_Display hex_digit_display_19 (.value(register_4_q_3));  // open: dp
  Counter #(.width(12), .max('hfff)) counter_2 (
    .load(and_1_out), .D({register_5_q_3, register_5_q_2}), .count(and_2_out), .Q(counter_2_q),
    .clk(clock_1_out), .clr(button_1_out));  // open: carry
  Hex_Digit_Display hex_digit_display_20 (.value(register_4_q));  // open: dp
  Multiplexer #(.width(12), .enable("false")) multiplexer_3 (
    .in0({register_5_q_3, register_5_q_2}), .in1(counter_2_q),
    .out({multiplexer_3_out_3, multiplexer_3_out_2, multiplexer_3_out}), .sel(nor_1_out));
  LED led_1 (.in(decoder_3_out0));
  LED led_2 (.in(decoder_3_out1));
  LED led_3 (.in(decoder_3_out2));
  LED led_4 (.in(decoder_3_out3));
  Hex_Digit_Display hex_digit_display_21 (.value(multiplexer_3_out_3));  // open: dp
  Hex_Digit_Display hex_digit_display_22 (.value(multiplexer_3_out));  // open: dp
  Hex_Digit_Display hex_digit_display_23 (.value(multiplexer_3_out_2));  // open: dp
  RAM #(.addrWidth(12), .dataWidth(16), .bus("separate")) ram_1 (
    .addr({multiplexer_3_out_3, multiplexer_3_out_2, multiplexer_3_out}),
    .din({register_4_q_4, register_4_q_3, register_4_q_2, register_4_q}), .data(ram_1_data),
    .str(decoder_2_out2), .sel(1'b1), .clk(clock_1_out));  // open: ld, clr
  Hex_Digit_Display hex_digit_display_24 (.value(ram_1_data[15:12]));  // open: dp
  Hex_Digit_Display hex_digit_display_25 (.value(ram_1_data[11:8]));  // open: dp
  Hex_Digit_Display hex_digit_display_26 (.value(ram_1_data[7:4]));  // open: dp
  Hex_Digit_Display hex_digit_display_27 (.value(ram_1_data[3:0]));  // open: dp

  // Notes on the sheet:
  //   Seleciona destino
  //   Seleciona origem
  //   Carga da memória
  //   TRA
  //   RESET
  //   CLOCK
  //   Carga de outro registrador
  //   Acumulador
  //   Registrador de Instruções
  //   OpCode
  //   Endereço
  //   NOP
  //   JMP
  //   LDA
  //   ver explicação para esta logica em README.md 2021-05-06
  //   Busca de instrução
  //   STA
  //   Atualiza PC
  //   Contador de Programa
  //   Expõe endereço de operando ou PC
  //   Se busca instrução, desabilita outras instruções. Tem que habilitar para buscar operando na memória
  //   Endereço Exposto
  //   Busca de instrução
  //   Executa instrução
  //   Atualiza PC
  //   Dados da memória
endmodule
